# Fritzing sketch Flying_Fish_Demo (saved by Fritzing 0.9.3b)
breadboards: 1

parts:
  Bauteil1 = Arduino Uno (Rev3)
  LED1 = RGB LED (com. cathode, rgb) [package="5 mm [THT]"]
  LED2 = RGB LED (com. cathode, rgb) [package="5 mm [THT]"]

nets:
  N1: Bauteil1.D8, LED2.red_anode
  N2: Bauteil1.D9_PWM, LED2.common_cathode
  N3: Bauteil1.D10_PWM/SS, LED2.blue_anode
  N4: Bauteil1.D11_PWM/MOSI, LED1.red_anode
  N5: Bauteil1.D12/MISO, LED1.common_cathode
  N6: Bauteil1.D13/SCK, LED1.blue_anode
  N7: Bauteil1.GND, LED1.green_anode, LED2.green_anode
